// Logisim project CombinationLock.circ as structural Verilog: 1 circuit, main circuit main
module main (
);

  wire and_1_out, Button01_out, Button02_out, Button04_out, Button4_out, comparator_1_eq, comparator_2_eq,
       comparator_3_eq, comparator_4_eq, Reset_out;
  wire [3:0] counter_1_q, counter_2_q, counter_3_q, counter_4_q, Digit01Code_sw4, Digit02Code_sw4,
       Digit03Code_sw4, Digit04Code_sw4;

  Counter #(.max('h9), .width(4)) counter_1 (
    .clr(Reset_out), .clk(Button01_out), .Q(counter_1_q));  // open: load, up, count, D, carry
  Counter #(.max('h9), .width(4)) counter_2 (
    .clr(Reset_out), .clk(Button4_out), .Q(counter_2_q));  // open: load, up, count, D, carry
  Button Reset (.out(Reset_out));
  Hex_Digit_Display Digit01 (.value(counter_1_q));  // open: dp
  Button Button01 (.out(Button01_out));
  Hex_Digit_Display Digit02 (.value(counter_3_q));  // open: dp
  Hex_Digit_Display Digit03 (.value(counter_2_q));  // open: dp
  Button Button02 (.out(Button02_out));
  DipSwitch #(.number(4)) Digit01Code (
    .sw1(Digit01Code_sw4[3]), .sw2(Digit01Code_sw4[2]), .sw3(Digit01Code_sw4[1]), .sw4(Digit01Code_sw4[0]));
  LED Unlocked (.in(and_1_out));
  Hex_Digit_Display Digit04 (.value(counter_4_q));  // open: dp
  Button Button4 (.out(Button4_out));
  Button Button04 (.out(Button04_out));
  Comparator #(.width(4)) comparator_1 (.a(Digit01Code_sw4), .b(counter_1_q), .eq(comparator_1_eq));  // open: gt, lt
  and and_1 (and_1_out, comparator_1_eq, comparator_3_eq, comparator_4_eq, comparator_2_eq);
  Comparator #(.width(4)) comparator_2 (.a(Digit04Code_sw4), .b(counter_2_q), .eq(comparator_2_eq));  // open: gt, lt
  DipSwitch #(.number(4)) Digit04Code (
    .sw1(Digit04Code_sw4[3]), .sw2(Digit04Code_sw4[2]), .sw3(Digit04Code_sw4[1]), .sw4(Digit04Code_sw4[0]));
  Counter #(.max('h9), .width(4)) counter_3 (
    .clr(Reset_out), .clk(Button02_out), .Q(counter_3_q));  // open: load, up, count, D, carry
  Counter #(.max('h9), .width(4)) counter_4 (
    .clr(Reset_out), .clk(Button04_out), .Q(counter_4_q));  // open: load, up, count, D, carry
  DipSwitch #(.number(4)) Digit03Code (
    .sw1(Digit03Code_sw4[3]), .sw2(Digit03Code_sw4[2]), .sw3(Digit03Code_sw4[1]), .sw4(Digit03Code_sw4[0]));
  Comparator #(.width(4)) comparator_3 (.a(Digit02Code_sw4), .b(counter_3_q), .eq(comparator_3_eq));  // open: gt, lt
  DipSwitch #(.number(4)) Digit02Code (
    .sw1(Digit02Code_sw4[3]), .sw2(Digit02Code_sw4[2]), .sw3(Digit02Code_sw4[1]), .sw4(Digit02Code_sw4[0]));
  Comparator #(.width(4)) comparator_4 (.a(Digit03Code_sw4), .b(counter_4_q), .eq(comparator_4_eq));  // open: gt, lt
endmodule
